# Fritzing sketch Vitrine_Fan_Control (saved by Fritzing 0.9.9b)

parts:
  R2 = Resistor [tolerance=±1% power=0.25 resistance=2.2k package=THT]  # not connected
  ESP32_D1_Mini = MH-ET Live Minikit for ESP32
  PWM_Fan_(+5V)_-_Noctua_NF-F12_5V_PWM = Fan - 4 wire [package=THT]
  SHT31-D = Adafruit SHT31-D

nets:
  GND: ESP32_D1_Mini.GND, PWM_Fan_(+5V)_-_Noctua_NF-F12_5V_PWM.GND, SHT31-D.GND
  3.3V: ESP32_D1_Mini.3.3V, SHT31-D.VCC
  N1: ESP32_D1_Mini.IO22, SHT31-D.SCL
  N2: ESP32_D1_Mini.IO21, SHT31-D.SDA
  N3: ESP32_D1_Mini.IO17, PWM_Fan_(+5V)_-_Noctua_NF-F12_5V_PWM.Tach
  N4: ESP32_D1_Mini.IO16, PWM_Fan_(+5V)_-_Noctua_NF-F12_5V_PWM.PWM
  N5: ESP32_D1_Mini.VCC, PWM_Fan_(+5V)_-_Noctua_NF-F12_5V_PWM.Power

custom parts:
  MH-ET Live Minikit for ESP32: MH-ET Live Minikit for ESP32 ( http://mh.nodebb.com/topic/8/mh-et-live-minikit-for-esp32/2/) PCB footprint is invalid.
  Fan - 4 wire: Fan, 4 wire with tach.
  Adafruit SHT31-D: Sensirion Temperature/Humidity sensors are some of the finest & highest-accuracy devices you can get. And, finally we have some that have a true I2C interface for easy reading. The SHT31-D sensor has an excellent ±2% relative humidity and ±0.3°C accuracy for most uses. We now use the version with a PTFE filter, it'll stay clean while still allowing humidity measurements to work Unlike earlier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
